# Fritzing sketch IR_beacon (saved by Fritzing 1.0.4)
breadboards: 1

parts:
  Propeller1 = Parallax Propeller D40 [package="DIP [THT]"]
  IR_Led-TSAL6100 = LEDs [package=led10mm]
  IRLZ44N_Mosfet = MOSFET-NCHANNEL [package=to-92]
  R1 = Resistor [tolerance=±5% resistance=2.2 package="0402 [SMD]"]
  R2 = Resistor [tolerance=±5% resistance=10k package="0402 [SMD]"]

nets:
  N1: Propeller1.VSS, IRLZ44N_Mosfet.D, R2.Pin_1
  N2: Propeller1.VDD#11, R1.Pin_1
  N3: Propeller1.P11, IRLZ44N_Mosfet.G, R2.Pin_0
  N4: IR_Led-TSAL6100.C, R1.Pin_0
  N5: IR_Led-TSAL6100.A, IRLZ44N_Mosfet.S
