# Fritzing sketch ice_robot (saved by Fritzing 1.0.4)
breadboards: 1

parts:
  Particle_Photon_2_(powered_through_USB) = photon2
  Lid_servo = Basic Servo
  IR1_Left = TSOP312.., 314.. [package=THT]
  IR2_Right = TSOP312.., 314.. [package=THT]
  Right_motors_(via_HB-25_controller) = Servo Improved
  Left_motors_(via_HB-25_controller) = Servo Improved
  VCC1 = 4 x AAA Battery Mount [internal_resistance=0.1Ω]
  R1 = Resistor [tolerance=±5% power=0.25W resistance=10k package=THT]
  R2 = Resistor [tolerance=±5% power=0.25W resistance=10k package=THT]

nets:
  N1: Particle_Photon_2_(powered_through_USB).Pin_2, Particle_Photon_2_(powered_through_USB).Pin_31, IR1_Left.Vs, IR2_Right.Vs
  GND: Particle_Photon_2_(powered_through_USB).Pin_4, Particle_Photon_2_(powered_through_USB).Pin_30, Particle_Photon_2_(powered_through_USB).Pin_32, Lid_servo.gnd, IR1_Left.GND, IR2_Right.GND, Right_motors_(via_HB-25_controller).ground, Left_motors_(via_HB-25_controller).ground, VCC1.-
  N2: Particle_Photon_2_(powered_through_USB).Pin_12, Left_motors_(via_HB-25_controller).signal
  N3: Particle_Photon_2_(powered_through_USB).Pin_13, Lid_servo.pulse
  N4: Particle_Photon_2_(powered_through_USB).Pin_18, Right_motors_(via_HB-25_controller).signal
  N5: Particle_Photon_2_(powered_through_USB).Pin_19, R2.Pin_0
  N6: Particle_Photon_2_(powered_through_USB).Pin_25, R1.Pin_0
  N7: Particle_Photon_2_(powered_through_USB).Pin_26, Lid_servo.vcc
  N8: Particle_Photon_2_(powered_through_USB).Pin_28, Particle_Photon_2_(powered_through_USB).Pin_29
  N9: IR1_Left.Data, R2.Pin_1
  N10: IR2_Right.Data, R1.Pin_1

custom parts:
  photon2: The Photon 2 is a development module with a microcontroller and Wi-Fi networking.
